// Digital circuit lutcomp.dig as structural Verilog
module lutcomp (
  input  RESET,
  input  clk
);

  wire CLK_t, CLK_t_t, HALT, not_2_out, switch_1_b, uc_1_p4, uc_1_p5, uc_1_p6, uc_1_p7, uc_1_p8, uc_1_p9,
       uc_1_p10, uc_1_p11, uc_1_p12, uc_1_p13, uc_1_p14, uc_1_p15, uc_1_p16, uc_1_p17, uc_1_p19, uc_1_p20,
       uc_1_p21, undriven, undriven_2, undriven_3, undriven_4, undriven_5, undriven_6, undriven_7, undriven_8;
  wire [6:0] uc_1_p3;
  wire [7:7] uc_1_p3_2;
  wire [23:0] pc_1_pc;

  and and_1 (CLK_t, clk, HALT);
  not not_1 (CLK_t_t, CLK_t);
  // uc uc_1: pin names not known; wires that end beside it: CLK_t_t, RESET, {uc_1_p3_2[7], uc_1_p3}, uc_1_p4, uc_1_p5, uc_1_p6, uc_1_p7, uc_1_p8, uc_1_p9, uc_1_p10, uc_1_p11, uc_1_p12, uc_1_p13, uc_1_p14, uc_1_p15, uc_1_p16, uc_1_p17, HALT, uc_1_p19, uc_1_p20, uc_1_p21
  not not_2 (not_2_out, uc_1_p4);
  // Probe on undriven_5
  // Probe on undriven_6
  // Probe on undriven_7
  // Probe on undriven_8
  pc pc_1 (.PC_INC(uc_1_p6), .RESET(RESET), .PC_SPE(uc_1_p21), .OE(not_2_out), .PC(pc_1_pc));  // open: ADDR
  Switch switch_1 (.A(uc_1_p17), .B(switch_1_b));
  Terminal terminal_1 (.D({1'b0, uc_1_p3}), .C(uc_1_p17), .en(1'b1));
  Break #(.Cycles(10000000)) BREAK_ON_TTYOUT (.brk(switch_1_b));
  memory memory_1 (
    .MEM_CP(uc_1_p9), .ADDR_OE(uc_1_p4), .A0_CP(uc_1_p14), .A1_CP(uc_1_p15), .A2_CP(uc_1_p16),
    .MEM_OE(uc_1_p20), .DATA({uc_1_p3_2[7], uc_1_p3}), .ADDR(pc_1_pc));  // open: DATA_2, DATA_OE
  \reg  W (.IO({uc_1_p3_2[7], uc_1_p3}), .OE(undriven), .CP(uc_1_p10));
  \reg  X (.IO({uc_1_p3_2[7], uc_1_p3}), .OE(undriven_2), .CP(uc_1_p11));
  \reg  Y (.IO({uc_1_p3_2[7], uc_1_p3}), .OE(undriven_3), .CP(uc_1_p12));
  \reg  Z (.IO({uc_1_p3_2[7], uc_1_p3}), .OE(undriven_4), .CP(uc_1_p13));
  // alu alu_1: pin names not known; wires that end beside it: uc_1_p5, uc_1_p19, uc_1_p8, uc_1_p7, {uc_1_p3_2[7], uc_1_p3}

  // Notes on the sheet:
  //   RESET: default 1
  //   clk: Hz: 10000
  //   4A
  //   4B
  //   4Y
  //   6A
  //   6Y
  //   3A
  //   3Y
endmodule
